# Fritzing sketch shield (saved by Fritzing 0.8.5b)
circuit board: 8.46667cm x 5.64444cm

parts:
  M1 = DC Motor
  M2 = Stepper Motor - Bipolar
  Componente1 = Arduino Uno (Rev3)
  IC1 = L293D [package=THT]
  J1 = Screw terminal - 2 pins [package=THT]
  J2 = Screw terminal - 2 pins [package=THT]
  J3 = screw terminal, 4 pins
  Power_plug1 = Power plug
  Pololu_A1 = Pololu A4988 [package=SO16]
  C1 = Electrolytic Capacitor [capacitance=0.22mF voltage=63V package="100 mil [THT, electrolytic]"]

nets:
  N1: M1.pin_1, IC1.Out_2_(_Controlled_by_Enable_1_), IC1.Out_3_(_Controlled_by_Enable_2_), J1.pin1, C1.-
  N2: M1.pin_2, IC1.Out_1_(_Controlled_by_Enable_1_), IC1.Out_4_(_Controlled_by_Enable_2_), J1.pin2
  N3: M2.A, J3.pin4, Pololu_A1.2B
  N4: M2.C, J3.pin3, Pololu_A1.2A
  N5: M2.B, J3.pin2, Pololu_A1.1B
  N6: M2.D, J3.pin1, Pololu_A1.1A
  N7: Componente1.D12/MISO, Pololu_A1.DIR
  N8: Componente1.D3_PWM, Pololu_A1.STEP
  N9: Componente1.D5_PWM, IC1.In_1, IC1.In_4
  N10: Componente1.D6_PWM, IC1.Enable_1, IC1.Enable_2
  N11: Componente1.D7, IC1.In_2, IC1.In_3
  5V: Componente1.5V, IC1.+V, Pololu_A1.MS1, Pololu_A1.MS2, Pololu_A1.MS3, Pololu_A1.VDD
  GND: Componente1.GND, IC1.0V, J2.pin1, Power_plug1.GND, Pololu_A1.ENABLE, Pololu_A1.RESET, Pololu_A1.SLEEP, Pololu_A1.GND
  N12: IC1.+Vmotor, J2.pin2, Power_plug1.VCC, Pololu_A1.VMOT

custom parts:
  Pololu A4988: The A4988 stepper motor driver carrier is a breakout board for Allegro’s A4988 microstepping bipolar stepper motor driver. The driver features adjustable current limiting, overcurrent and overtemperature protection, and five different microstep resolutions (down to 1/16-step). It operates from 8 – 35 V and can deliver up to approximately 1 A per phase without a heat sink or forced air flow (it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
